// Logisim project Practica5.circ as structural Verilog: 5 circuits, main circuit SEGMENTADO
module BR32 (
  input  CLK,
  input  Reset,
  input  [31:0] DATA,
  input  RegWR,
  input  [4:0] RS__A,
  input  [4:0] RD,
  input  [4:0] RT_B,
  output [31:0] BusA,
  output [31:0] BusB
);

  wire decoder_1_out0, decoder_1_out1, decoder_1_out2, decoder_1_out3, decoder_1_out4, decoder_1_out5,
       decoder_1_out6, decoder_1_out7;
  wire [31:0] br4_1_a, br4_1_b, br4_2_a, br4_2_b, br4_3_a, br4_3_b, br4_4_a, br4_4_b, br4_5_a, br4_5_b,
       br4_6_a, br4_6_b, br4_7_a, br4_7_b, br4_8_a, br4_8_b;

  Decoder #(.select(3), .disabled(0)) decoder_1 (
    .out0(decoder_1_out0), .out1(decoder_1_out1), .out2(decoder_1_out2), .out3(decoder_1_out3),
    .out4(decoder_1_out4), .out5(decoder_1_out5), .out6(decoder_1_out6), .out7(decoder_1_out7),
    .sel(RD[4:2]), .en(RegWR));
  BR4 br4_1 (
    .DATA(DATA), .RegWR(decoder_1_out0), .RD(RD[1:0]), .A(br4_1_a), .B(br4_1_b), .CLK(CLK), .Reset(Reset),
    .RS(RS__A[1:0]), .RT(RT_B[1:0]));
  BR4 br4_2 (
    .DATA(DATA), .RegWR(decoder_1_out1), .RD(RD[1:0]), .A(br4_2_a), .B(br4_2_b), .CLK(CLK), .Reset(Reset),
    .RS(RS__A[1:0]), .RT(RT_B[1:0]));
  BR4 br4_3 (
    .DATA(DATA), .RegWR(decoder_1_out2), .RD(RD[1:0]), .A(br4_3_a), .B(br4_3_b), .CLK(CLK), .Reset(Reset),
    .RS(RS__A[1:0]), .RT(RT_B[1:0]));
  BR4 br4_4 (
    .DATA(DATA), .RegWR(decoder_1_out3), .RD(RD[1:0]), .A(br4_4_a), .B(br4_4_b), .CLK(CLK), .Reset(Reset),
    .RS(RS__A[1:0]), .RT(RT_B[1:0]));
  BR4 br4_5 (
    .DATA(DATA), .RegWR(decoder_1_out4), .RD(RD[1:0]), .A(br4_5_a), .B(br4_5_b), .CLK(CLK), .Reset(Reset),
    .RS(RS__A[1:0]), .RT(RT_B[1:0]));
  BR4 br4_6 (
    .DATA(DATA), .RegWR(decoder_1_out5), .RD(RD[1:0]), .A(br4_6_a), .B(br4_6_b), .CLK(CLK), .Reset(Reset),
    .RS(RS__A[1:0]), .RT(RT_B[1:0]));
  BR4 br4_7 (
    .DATA(DATA), .RegWR(decoder_1_out6), .RD(RD[1:0]), .A(br4_7_a), .B(br4_7_b), .Reset(Reset),
    .RS(RS__A[1:0]), .RT(RT_B[1:0]));  // open: CLK
  BR4 br4_8 (
    .DATA(DATA), .RegWR(decoder_1_out7), .RD(RD[1:0]), .A(br4_8_a), .B(br4_8_b), .CLK(CLK), .Reset(Reset),
    .RS(RS__A[1:0]), .RT(RT_B[1:0]));
  Multiplexer #(.select(3), .width(32), .enable("false")) multiplexer_1 (
    .in0(br4_1_a), .in1(br4_2_a), .in2(br4_3_a), .in3(br4_4_a), .in4(br4_5_a), .in5(br4_6_a), .in6(br4_7_a),
    .in7(br4_8_a), .out(BusA), .sel(RS__A[4:2]));
  Multiplexer #(.select(3), .width(32), .enable("false")) multiplexer_2 (
    .in0(br4_1_b), .in1(br4_2_b), .in2(br4_3_b), .in3(br4_4_b), .in4(br4_5_b), .in5(br4_6_b), .in6(br4_7_b),
    .in7(br4_8_b), .out(BusB), .sel(RT_B[4:2]));
endmodule

module BR4 (
  input  [1:0] RS,
  input  CLK,
  input  Reset,
  input  [31:0] DATA,
  input  RegWR,
  input  [1:0] RD,
  input  [1:0] RT,
  output [31:0] A,
  output [31:0] B
);

  wire decoder_1_out0, decoder_1_out1, decoder_1_out2, decoder_1_out3;
  wire [31:0] register_1_q, register_2_q, register_3_q, register_4_q;

  Decoder #(.select(2), .disabled(0)) decoder_1 (
    .out0(decoder_1_out0), .out1(decoder_1_out1), .out2(decoder_1_out2), .out3(decoder_1_out3), .sel(RD),
    .en(RegWR));
  Register #(.width(32), .trigger("falling")) register_1 (
    .D(DATA), .en(decoder_1_out0), .Q(register_1_q), .clk(CLK), .clr(Reset));
  Register #(.width(32), .trigger("falling")) register_2 (
    .D(DATA), .en(decoder_1_out1), .Q(register_2_q), .clk(CLK), .clr(Reset));
  Register #(.width(32), .trigger("falling")) register_3 (
    .D(DATA), .en(decoder_1_out2), .Q(register_3_q), .clk(CLK), .clr(Reset));
  Register #(.width(32), .trigger("falling")) register_4 (
    .D(DATA), .en(decoder_1_out3), .Q(register_4_q), .clk(CLK), .clr(Reset));
  Multiplexer #(.select(2), .width(32), .enable("false")) multiplexer_1 (
    .in0(register_1_q), .in1(register_2_q), .in2(register_3_q), .in3(register_4_q), .out(A), .sel(RS));
  Multiplexer #(.select(2), .width(32), .enable("false")) multiplexer_2 (
    .in0(register_1_q), .in1(register_2_q), .in2(register_3_q), .in3(register_4_q), .out(B), .sel(RT));
endmodule

module SEGMENTADO (
  input  Reset,
  output [31:0] BusA,
  output [31:0] BusA_2
);

  wire AND, AND2, and_1_out, BEQ, CLK, habilitarMEN, ID_EX_BEQ, ID_RD_WR, IDhabilitarMEN, MuxBR32, MuxEX,
       MuxPC, MuxRW, MuxUC, not_1_out, PC, RD_WR, RegWr_MEN, RegWr_WB;
  wire [1:0] ID_EX_q, uni_anticipacion_op_1_out_7, uni_anticipacion_op_1_out_8;
  wire [1:1] EX_MEN_q;
  wire [2:0] UC;
  wire [4:0] IF_RA, IF_RB, multiplexer_4_out, RA, RB, RW, RW2, RW_MEN;
  wire [6:0] multiplexer_3_out, rom_2_data;
  wire [9:0] ID_EX_3_q;
  wire [10:0] register_1_q_2;
  wire [15:0] counter_1_q, ID_EX_2_q, Mux1;
  wire [31:0] A, adder_1_out, B, bit_extender_1_out, br32_1_busa, br32_1_busb, Data, EX_MEN_2_q, EX_MEN_3_q,
       MEMORIA, MEN, multiplexer_5_out, ram_1_data, register_6_q, rom_1_data, SUMADOR_MOV;
  wire [31:29] register_1_q;

  Multiplexer #(.select(2), .width(32), .enable("false")) multiplexer_1 (
    .in0(A), .in1(MEN), .in2(Data), .out(BusA), .sel(uni_anticipacion_op_1_out_8));  // open: in3
  UNI_ANTICIPACION_OP uni_anticipacion_op_1 (
    .RegWr_MEN(RegWr_MEN), .RA(RA), .RB(RB), .RegWr_WB(RegWr_WB), .RW_WB(RW), .RW_MEN(RW_MEN),
    .out_7(uni_anticipacion_op_1_out_7), .out_8(uni_anticipacion_op_1_out_8));
  not not_1 (not_1_out, MuxPC);
  and and_1 (and_1_out, PC, not_1_out);
  Counter #(.width(16), .max('hffff)) counter_1 (
    .load(MuxPC), .D(Mux1), .count(and_1_out), .Q(counter_1_q), .clk(CLK), .clr(Reset));  // open: carry
  Multiplexer #(.select(2), .width(32), .enable("false")) multiplexer_2 (
    .in0(B), .in1(MEN), .in2(Data), .out(BusA_2), .sel(uni_anticipacion_op_1_out_7));  // open: in3
  Clock Reloj (.out(CLK));
  ROM #(.addrWidth(16), .dataWidth(32)) rom_1 (.addr(counter_1_q), .data(rom_1_data), .sel(1'b1));
  UNI_DETENCION uni_detencion_1 (
    .IF_ID_RA(IF_RA), .ID_EX_RB(RB), .IF_ID_RB(IF_RB), .ID_EX_HabilitarMEN(IDhabilitarMEN),
    .ID_EX_RD_WR(ID_RD_WR), .MuXUC(MuxUC), .PC(PC), .ID_EX_BEQ(ID_EX_BEQ), .EX_MEN_BEQ(BEQ));
  Register #(.width(32), .trigger("falling")) register_1 (
    .D(rom_1_data), .en(PC), .Q({register_1_q, UC, IF_RA, IF_RB, RW2, register_1_q_2}), .clk(CLK), .clr(Reset));
  ROM #(.addrWidth(3), .dataWidth(7)) rom_2 (.addr(UC), .data(rom_2_data));  // open: sel
  assign bit_extender_1_out = {{16{1'b0}}, {RW2, register_1_q_2}};  // Bit_Extender bit_extender_1
  Multiplexer #(.width(7), .enable("false")) multiplexer_3 (
    .in0(rom_2_data), .in1({7{1'b0}}), .out(multiplexer_3_out), .sel(MuxUC));
  BR32 br32_1 (
    .RS__A(IF_RA), .DATA(Data), .RegWR(RegWr_WB), .RD(RW), .RT_B(IF_RB), .BusA(br32_1_busa),
    .BusB(br32_1_busb), .Reset(Reset), .CLK(CLK));
  Register #(.width(7)) ID_EX (
    .D(multiplexer_3_out), .en(1'b1), .Q({MuxRW, MuxEX, ID_EX_BEQ, IDhabilitarMEN, ID_RD_WR, ID_EX_q}),
    .clk(CLK), .clr(Reset));
  Register #(.width(5)) register_2 (.D(IF_RB), .en(1'b1), .Q(RB), .clk(CLK), .clr(Reset));
  Register #(.width(5)) register_3 (.D(IF_RA), .en(1'b1), .Q(RA), .clk(CLK), .clr(Reset));
  Register #(.width(32)) register_4 (.D(br32_1_busa), .en(1'b1), .Q(A), .clk(CLK), .clr(Reset));
  Register #(.width(32)) register_5 (.D(br32_1_busb), .en(1'b1), .Q(B), .clk(CLK), .clr(Reset));
  Register #(.width(32)) register_6 (.D(bit_extender_1_out), .en(1'b1), .Q(register_6_q), .clk(CLK), .clr(Reset));
  Register #(.width(16)) ID_EX_2 (.D({RW2, register_1_q_2}), .en(1'b1), .Q(ID_EX_2_q), .clk(CLK), .clr(Reset));
  Register #(.width(10)) ID_EX_3 (.D({RW2, IF_RB}), .en(1'b1), .Q(ID_EX_3_q), .clk(CLK), .clr(Reset));
  Multiplexer #(.width(5), .enable("false")) multiplexer_4 (
    .in0(ID_EX_3_q[4:0]), .in1(ID_EX_3_q[9:5]), .out(multiplexer_4_out), .sel(MuxRW));
  Adder #(.width(32)) adder_1 (.a(BusA), .b(BusA_2), .out(adder_1_out));  // open: cin, cout
  Comparator #(.width(32)) comparator_1 (.a(BusA), .b(BusA_2), .eq(AND));  // open: gt, lt
  Multiplexer #(.width(32), .enable("false")) multiplexer_5 (
    .in0(adder_1_out), .in1(register_6_q), .out(multiplexer_5_out), .sel(MuxEX));
  Register #(.width(5)) EX_MEN (
    .D({ID_EX_BEQ, IDhabilitarMEN, ID_RD_WR, ID_EX_q}), .en(1'b1),
    .Q({BEQ, habilitarMEN, RD_WR, EX_MEN_q[1], RegWr_MEN}), .clk(CLK), .clr(Reset));
  Register #(.width(32)) EX_MEN_2 (.D(A), .en(1'b1), .Q(EX_MEN_2_q), .clk(CLK), .clr(Reset));
  Register #(.width(32)) EX_MEN_3 (.D(B), .en(1'b1), .Q(EX_MEN_3_q), .clk(CLK), .clr(Reset));
  Register #(.width(32)) EX_MEN_4 (.D(multiplexer_5_out), .en(1'b1), .Q(MEN), .clk(CLK), .clr(Reset));
  Register #(.width(1)) EX_MEN_5 (.D(AND), .en(1'b1), .Q(AND2), .clk(CLK), .clr(Reset));
  Register #(.width(16)) EX_MEN_6 (.D(ID_EX_2_q), .en(1'b1), .Q(Mux1), .clk(CLK), .clr(Reset));
  Register #(.width(5)) EX_MEN_7 (.D(multiplexer_4_out), .en(1'b1), .Q(RW_MEN), .clk(CLK), .clr(Reset));
  RAM #(.addrWidth(16), .dataWidth(32), .bus("separate")) ram_1 (
    .addr(EX_MEN_2_q[15:0]), .din(EX_MEN_3_q), .data(ram_1_data), .str(RD_WR), .sel(habilitarMEN), .clk(CLK),
    .ld(habilitarMEN));  // open: clr
  and and_2 (MuxPC, BEQ, AND2);
  Register #(.width(2)) MEN_WB (
    .D({EX_MEN_q[1], RegWr_MEN}), .en(1'b1), .Q({MuxBR32, RegWr_WB}), .clk(CLK), .clr(Reset));
  Register #(.width(32)) MEN_WB_2 (.D(ram_1_data), .en(1'b1), .Q(MEMORIA), .clk(CLK), .clr(Reset));
  Register #(.width(32)) MEN_WB_3 (.D(MEN), .en(1'b1), .Q(SUMADOR_MOV), .clk(CLK), .clr(Reset));
  Register #(.width(5)) MEN_WB_4 (.D(RW_MEN), .en(1'b1), .Q(RW), .clk(CLK), .clr(Reset));
  Multiplexer #(.width(32), .enable("false")) multiplexer_6 (
    .in0(SUMADOR_MOV), .in1(MEMORIA), .out(Data), .sel(MuxBR32));

  // Other names for the same wires on the sheet: RW1[4:0] = IF_RB; OP1[31:0] = BusA; OP2[31:0] = BusA_2;
  //   RW_WB[4:0] = RW; WB[31:0] = Data

  // Notes on the sheet:
  //   PC
  //   Memoria Instucciones
  //   contents of rom_1 (hex, n*v repeats v):
  //   0 4000001 4020006 4030007 8240000 14200800 14a42800 10220009 10000004 c650000
  //   IF/ID
  //   (21-25)
  //   (16-20)
  //   (11-15)
  //   INMEDIATO (0-15)
  //   UNIDAD DE CONTROL
  //   contents of rom_2 (hex, n*v repeats v):
  //   0 21 b c 10 41
  //   DIR.SALTO CONDICIONAL
  //   REGISTRO DESTINO (RW)
  //   ID/EX
  //   ID/EX
  //   ID/EX
  //   ID/EX
  //   ID/EX
  //   Memoria Datos
  //   out = 0 escritura
endmodule

module UNI_ANTICIPACION_OP (
  input  [4:0] RA,
  input  [4:0] RW_MEN,
  input  [4:0] RW_WB,
  input  [4:0] RB,
  input  RegWr_MEN,
  input  RegWr_WB,
  output [1:0] out_7,
  output [1:0] out_8
);

  wire comparator_1_eq, comparator_2_eq, comparator_3_eq, comparator_4_eq;

  Comparator #(.width(5)) comparator_1 (.a(RW_MEN), .b(RA), .eq(comparator_1_eq));  // open: gt, lt
  Comparator #(.width(5)) comparator_2 (.a(RA), .b(RW_WB), .eq(comparator_2_eq));  // open: gt, lt
  and and_1 (out_8[0], RegWr_MEN, comparator_1_eq);
  and and_2 (out_8[1], comparator_2_eq, RegWr_WB);
  Comparator #(.width(5)) comparator_3 (.a(RW_MEN), .b(RB), .eq(comparator_3_eq));  // open: gt, lt
  Comparator #(.width(5)) comparator_4 (.a(RB), .b(RW_WB), .eq(comparator_4_eq));  // open: gt, lt
  and and_3 (out_7[0], RegWr_MEN, comparator_3_eq);
  and and_4 (out_7[1], comparator_4_eq, RegWr_WB);
endmodule

module UNI_DETENCION (
  input  ID_EX_BEQ,
  input  EX_MEN_BEQ,
  input  [4:0] IF_ID_RA,
  input  ID_EX_HabilitarMEN,
  input  [4:0] ID_EX_RB,
  input  ID_EX_RD_WR,
  input  [4:0] IF_ID_RB,
  output MuXUC,
  output PC
);

  wire and_1_out, and_3_out, and_4_out, comparator_1_eq, comparator_2_eq, not_1_out, not_2_out, not_3_out,
       or_1_out, or_3_out;

  Comparator #(.width(5)) comparator_1 (.a(IF_ID_RA), .b(ID_EX_RB), .eq(comparator_1_eq));  // open: gt, lt
  Comparator #(.width(5)) comparator_2 (.a(ID_EX_RB), .b(IF_ID_RB), .eq(comparator_2_eq));  // open: gt, lt
  or or_1 (or_1_out, ID_EX_BEQ, EX_MEN_BEQ);
  or or_2 (MuXUC, or_1_out, and_1_out);
  or or_3 (or_3_out, comparator_1_eq, comparator_2_eq);
  not not_1 (not_1_out, or_1_out);
  not not_2 (not_2_out, and_1_out);
  and and_1 (and_1_out, or_3_out, and_4_out);
  and and_2 (PC, not_1_out, not_2_out);
  and and_3 (and_3_out, 1'b1, ID_EX_HabilitarMEN);
  and and_4 (and_4_out, and_3_out, not_3_out);
  not not_3 (not_3_out, ID_EX_RD_WR);

  // Notes on the sheet:
  //   DETENCIÓN BEQ
  //   DETENCIÓN LOAD
endmodule
