// Logisim project ejer5.circ as structural Verilog: 1 circuit, main circuit main
module main (
  input  in_1,
  output out_2
);

  wire adder_1_cout, adder_1_out, and_1_out, clock_1_out, d_ff_1_q, d_ff_2_q, d_ff_3_q, not_1_out, not_2_out,
       or_1_out, or_2_out, or_3_out;

  D_Flip_Flop d_ff_1 (.clk(clock_1_out), .D(in_1), .Q(d_ff_1_q));  // open: Qn, preset, en, reset
  not not_1 (not_1_out, d_ff_1_q);
  Adder #(.width(1)) adder_1 (.a(d_ff_1_q), .b(d_ff_1_q), .out(adder_1_out), .cout(adder_1_cout));  // open: cin
  Clock clock_1 (.out(clock_1_out));
  or or_1 (or_1_out, adder_1_out, not_1_out);
  D_Flip_Flop d_ff_2 (.clk(clock_1_out), .D(or_1_out), .Q(d_ff_2_q));  // open: Qn, preset, en, reset
  D_Flip_Flop d_ff_3 (.clk(clock_1_out), .D(d_ff_2_q), .Q(d_ff_3_q));  // open: Qn, preset, en, reset
  not not_2 (not_2_out, d_ff_3_q);
  and and_1 (and_1_out, adder_1_cout, d_ff_3_q);
  or or_2 (or_2_out, not_2_out, adder_1_cout);
  or or_3 (or_3_out, and_1_out, or_2_out);
  J_K_Flip_Flop j_k_ff_1 (.J(or_3_out), .K(or_3_out), .Q(out_2));  // open: clk, Qn, preset, en, reset
endmodule
