// Logisim project ejer6.circ as structural Verilog: 1 circuit, main circuit main
module main (
  output out_1,
  output out_2,
  output out_3,
  output out_4
);

  wire clock_1_out, register_1_q, register_2_q, register_3_q, register_4_q;

  Clock clock_1 (.out(clock_1_out));
  Register #(.width(1)) register_1 (.D(out_4), .Q(register_1_q), .clk(clock_1_out));  // open: en, clr
  Register #(.width(1)) register_2 (.D(out_3), .Q(register_2_q), .clk(register_1_q));  // open: en, clr
  Register #(.width(1)) register_3 (.D(out_2), .Q(register_3_q), .clk(register_2_q));  // open: en, clr
  Register #(.width(1)) register_4 (.D(out_1), .Q(register_4_q), .clk(register_3_q));  // open: en, clr
  not not_1 (out_4, register_1_q);
  not not_2 (out_3, register_2_q);
  not not_3 (out_2, register_3_q);
  not not_4 (out_1, register_4_q);

  // Notes on the sheet:
  //   Hace el mismo funcionamiento que una tabla de verdad
endmodule
