// Logisim project ejer7.circ as structural Verilog: 1 circuit, main circuit main
module main (
  input  in_1
);

  wire and_1_out, and_2_out, clock_1_out, j_k_ff_1_q, j_k_ff_2_q, j_k_ff_3_q, j_k_ff_4_q, not_1_out,
       not_2_out, not_3_out, not_4_out;

  Clock clock_1 (.out(clock_1_out));
  J_K_Flip_Flop #(.trigger("falling")) j_k_ff_1 (
    .J(in_1), .clk(clock_1_out), .K(in_1), .Q(j_k_ff_1_q), .reset(not_1_out));  // open: Qn, preset, en
  not not_1 (not_1_out, in_1);
  J_K_Flip_Flop #(.trigger("falling")) j_k_ff_2 (
    .J(j_k_ff_1_q), .clk(clock_1_out), .K(j_k_ff_1_q), .Q(j_k_ff_2_q), .reset(not_2_out));  // open: Qn, preset, en
  not not_2 (not_2_out, in_1);
  and and_1 (and_1_out, j_k_ff_1_q, j_k_ff_2_q);
  J_K_Flip_Flop #(.trigger("falling")) j_k_ff_3 (
    .J(and_1_out), .clk(clock_1_out), .K(and_1_out), .Q(j_k_ff_3_q), .reset(not_3_out));  // open: Qn, preset, en
  not not_3 (not_3_out, in_1);
  and and_2 (and_2_out, and_1_out, j_k_ff_3_q);
  _7_Segment_Display u_7_segment_display_1 (
    .e(j_k_ff_4_q), .d(j_k_ff_3_q), .c(j_k_ff_2_q), .dp(j_k_ff_1_q));  // open: g, f, a, b
  J_K_Flip_Flop #(.trigger("falling")) j_k_ff_4 (
    .J(and_2_out), .clk(clock_1_out), .K(and_2_out), .Q(j_k_ff_4_q), .reset(not_4_out));  // open: Qn, preset, en
  not not_4 (not_4_out, in_1);
endmodule
