// Logisim project ejer8.circ as structural Verilog
module ALU (
  input  C,
  input  A,
  input  B,
  input  [1:0] in_4,
  output out_5,
  output out_6
);

  wire adder_1_out, and_1_out, or_1_out, xor_1_out;

  and and_1 (and_1_out, B, A);
  or or_1 (or_1_out, B, A);
  xor xor_1 (xor_1_out, B, A);
  Adder #(.width(1)) adder_1 (.a(B), .b(A), .out(adder_1_out), .cin(C), .cout(out_6));
  Multiplexer #(.select(2), .enable("false")) multiplexer_1 (
    .in0(and_1_out), .in1(or_1_out), .in2(xor_1_out), .in3(adder_1_out), .out(out_5), .sel(in_4));
endmodule

module ALU_4_BITS (
  input  [3:0] B,
  input  CARRY,
  input  [3:0] A,
  input  [1:0] _01_OR,
  output [3:0] out_5,
  output out_6
);

  wire _0_out_6, _1_out_6, _2_out_6;

  ALU _0 (.out_5(out_5[0]), .A(A[0]), .B(B[0]), .in_4(_01_OR), .C(CARRY), .out_6(_0_out_6));
  ALU _1 (.out_5(out_5[1]), .A(A[1]), .B(B[1]), .in_4(_01_OR), .C(_0_out_6), .out_6(_1_out_6));
  ALU _2 (.out_5(out_5[2]), .A(A[2]), .B(B[2]), .in_4(_01_OR), .C(_1_out_6), .out_6(_2_out_6));
  ALU _3 (.out_5(out_5[3]), .A(A[3]), .B(B[3]), .in_4(_01_OR), .C(_2_out_6), .out_6(out_6));

  // Notes on the sheet:
  //   00 AND
  //   10 XOR
  //   11 SUMA
endmodule

module ALU_32_BITS (
  input  [31:0] B,
  input  [1:0] DECISION,
  input  [31:0] A,
  output [31:0] out_4,
  output out_5
);

  wire alu_4_bits_1_out_6, alu_4_bits_2_out_6, alu_4_bits_3_out_6, alu_4_bits_4_out_6, alu_4_bits_5_out_6,
       alu_4_bits_6_out_6, alu_4_bits_7_out_6;

  ALU_4_BITS alu_4_bits_1 (
    .B(B[3:0]), .A(A[3:0]), .out_5(out_4[3:0]), .out_6(alu_4_bits_1_out_6), ._01_OR(DECISION));  // open: CARRY
  ALU_4_BITS alu_4_bits_2 (
    .B(B[19:16]), .CARRY(alu_4_bits_7_out_6), .A(A[19:16]), .out_5(out_4[19:16]), .out_6(alu_4_bits_2_out_6),
    ._01_OR(DECISION));
  ALU_4_BITS alu_4_bits_3 (
    .B(B[7:4]), .CARRY(alu_4_bits_1_out_6), .A(A[7:4]), .out_5(out_4[7:4]), .out_6(alu_4_bits_3_out_6),
    ._01_OR(DECISION));
  ALU_4_BITS alu_4_bits_4 (
    .B(B[23:20]), .CARRY(alu_4_bits_2_out_6), .A(A[23:20]), .out_5(out_4[23:20]), .out_6(alu_4_bits_4_out_6),
    ._01_OR(DECISION));
  ALU_4_BITS alu_4_bits_5 (
    .B(B[11:8]), .CARRY(alu_4_bits_3_out_6), .A(A[11:8]), .out_5(out_4[11:8]), .out_6(alu_4_bits_5_out_6),
    ._01_OR(DECISION));
  ALU_4_BITS alu_4_bits_6 (
    .B(B[27:24]), .CARRY(alu_4_bits_4_out_6), .A(A[27:24]), .out_5(out_4[27:24]), .out_6(alu_4_bits_6_out_6),
    ._01_OR(DECISION));
  ALU_4_BITS alu_4_bits_7 (
    .B(B[15:12]), .CARRY(alu_4_bits_5_out_6), .A(A[15:12]), .out_5(out_4[15:12]), .out_6(alu_4_bits_7_out_6),
    ._01_OR(DECISION));
  ALU_4_BITS alu_4_bits_8 (
    .B(B[31:28]), .CARRY(alu_4_bits_6_out_6), .A(A[31:28]), .out_5(out_4[31:28]), .out_6(out_5),
    ._01_OR(DECISION));
endmodule
