// Logisim project ejercicio3simplificado.circ as structural Verilog: 1 circuit, main circuit main
module main (
  input  a,
  input  b,
  input  c,
  input  d,
  output f
);

  wire and_1_out, not_1_out;

  not not_1 (not_1_out, a);
  and and_1 (and_1_out, c, d);
  or or_1 (f, not_1_out, and_1_out);
endmodule
