// Logisim project ejercicio3sinsimplificar.circ as structural Verilog: 1 circuit, main circuit main
module main (
  input  a,
  input  b,
  input  c,
  input  d,
  output f
);

  wire nand_1_out, nand_2_out, nand_3_out, not_1_out, not_2_out, not_3_out, not_4_out, not_5_out, or_1_out;

  not not_1 (not_1_out, c);
  not not_2 (not_2_out, c);
  not not_3 (not_3_out, b);
  not not_4 (not_4_out, c);
  not not_5 (not_5_out, a);
  nand nand_1 (nand_1_out, a, not_1_out, not_2_out);
  nand nand_2 (nand_2_out, b, c, not_3_out);
  nand nand_3 (nand_3_out, a, b, not_4_out, d);
  or or_1 (or_1_out, not_5_out, d);
  and and_1 (f, nand_1_out, nand_2_out, nand_3_out, or_1_out);
endmodule
