// Logisim project ejercicio4.circ as structural Verilog: 1 circuit, main circuit main
module main (
  input  a,
  input  b,
  input  c,
  input  d,
  output y
);

  wire and_1_out, and_2_out, and_3_out, not_1_out, not_2_out, not_3_out, not_4_out;

  not not_1 (not_1_out, a);
  not not_2 (not_2_out, b);
  and and_1 (and_1_out, not_1_out, not_2_out, c);
  and and_2 (and_2_out, b, not_3_out);
  not not_3 (not_3_out, d);
  not not_4 (not_4_out, b);
  and and_3 (and_3_out, a, not_4_out, d);
  or or_1 (y, and_1_out, and_2_out, and_3_out);
endmodule
