// Logisim project ejercicio9f1sinsimplificar.circ as structural Verilog: 1 circuit, main circuit main
module main (
  input  a,
  input  b,
  input  c,
  input  d,
  input  e,
  input  g,
  input  h,
  input  i,
  input  j,
  input  k,
  output f
);

  wire and_1_out, and_2_out, or_1_out, or_2_out, or_3_out, or_4_out;

  or or_1 (or_1_out, a, b);
  or or_2 (or_2_out, c, d);
  or or_3 (or_3_out, k, g);
  or or_4 (or_4_out, h, i);
  and and_1 (and_1_out, or_1_out, or_2_out, e);
  and and_2 (and_2_out, or_3_out, or_4_out, j);
  or or_5 (f, and_1_out, and_2_out);
endmodule
