// Logisim project ejercicio9f2sinsimplificar.circ as structural Verilog: 1 circuit, main circuit main
module main (
  input  a,
  input  b,
  input  c,
  input  d,
  input  e,
  input  g,
  input  h,
  input  i,
  input  j,
  input  k,
  output f
);

  wire and_1_out, and_2_out, and_3_out, and_4_out, and_5_out, and_6_out, and_7_out, and_8_out;

  and and_1 (and_1_out, e, a, c);
  and and_2 (and_2_out, e, a, d);
  and and_3 (and_3_out, e, b, c);
  and and_4 (and_4_out, e, b, d);
  and and_5 (and_5_out, j, k, h);
  and and_6 (and_6_out, j, k, i);
  and and_7 (and_7_out, j, g, h);
  and and_8 (and_8_out, j, g, i);
  or or_1 (f, and_1_out, and_2_out, and_3_out, and_4_out, and_5_out, and_6_out, and_7_out, and_8_out);
endmodule
