// Logisim project Practica3.circ as structural Verilog: 10 circuits, main circuit MULTICICLO
module BR32 (
  input  CLK,
  input  Reset,
  input  [31:0] DATA,
  input  RegWR,
  input  [4:0] RS__A,
  input  [4:0] RD,
  input  [4:0] RT_B,
  output [31:0] BusA,
  output [31:0] BusB
);

  wire decoder_1_out0, decoder_1_out1, decoder_1_out2, decoder_1_out3, decoder_1_out4, decoder_1_out5,
       decoder_1_out6, decoder_1_out7;
  wire [31:0] br4_1_a, br4_1_b, br4_2_a, br4_2_b, br4_3_a, br4_3_b, br4_4_a, br4_4_b, br4_5_a, br4_5_b,
       br4_6_a, br4_6_b, br4_7_a, br4_7_b, br4_8_a, br4_8_b;

  Decoder #(.select(3), .disabled(0)) decoder_1 (
    .out0(decoder_1_out0), .out1(decoder_1_out1), .out2(decoder_1_out2), .out3(decoder_1_out3),
    .out4(decoder_1_out4), .out5(decoder_1_out5), .out6(decoder_1_out6), .out7(decoder_1_out7),
    .sel(RD[4:2]), .en(RegWR));
  BR4 br4_1 (
    .DATA(DATA), .RegWR(decoder_1_out0), .RD(RD[1:0]), .A(br4_1_a), .B(br4_1_b), .CLK(CLK), .Reset(Reset),
    .RS(RS__A[1:0]), .RT(RT_B[1:0]));
  BR4 br4_2 (
    .DATA(DATA), .RegWR(decoder_1_out1), .RD(RD[1:0]), .A(br4_2_a), .B(br4_2_b), .CLK(CLK), .Reset(Reset),
    .RS(RS__A[1:0]), .RT(RT_B[1:0]));
  BR4 br4_3 (
    .DATA(DATA), .RegWR(decoder_1_out2), .RD(RD[1:0]), .A(br4_3_a), .B(br4_3_b), .CLK(CLK), .Reset(Reset),
    .RS(RS__A[1:0]), .RT(RT_B[1:0]));
  BR4 br4_4 (
    .DATA(DATA), .RegWR(decoder_1_out3), .RD(RD[1:0]), .A(br4_4_a), .B(br4_4_b), .CLK(CLK), .Reset(Reset),
    .RS(RS__A[1:0]), .RT(RT_B[1:0]));
  BR4 br4_5 (
    .DATA(DATA), .RegWR(decoder_1_out4), .RD(RD[1:0]), .A(br4_5_a), .B(br4_5_b), .CLK(CLK), .Reset(Reset),
    .RS(RS__A[1:0]), .RT(RT_B[1:0]));
  BR4 br4_6 (
    .DATA(DATA), .RegWR(decoder_1_out5), .RD(RD[1:0]), .A(br4_6_a), .B(br4_6_b), .CLK(CLK), .Reset(Reset),
    .RS(RS__A[1:0]), .RT(RT_B[1:0]));
  BR4 br4_7 (
    .DATA(DATA), .RegWR(decoder_1_out6), .RD(RD[1:0]), .A(br4_7_a), .B(br4_7_b), .Reset(Reset),
    .RS(RS__A[1:0]), .RT(RT_B[1:0]));  // open: CLK
  BR4 br4_8 (
    .DATA(DATA), .RegWR(decoder_1_out7), .RD(RD[1:0]), .A(br4_8_a), .B(br4_8_b), .CLK(CLK), .Reset(Reset),
    .RS(RS__A[1:0]), .RT(RT_B[1:0]));
  Multiplexer #(.select(3), .width(32), .enable("false")) multiplexer_1 (
    .in0(br4_1_a), .in1(br4_2_a), .in2(br4_3_a), .in3(br4_4_a), .in4(br4_5_a), .in5(br4_6_a), .in6(br4_7_a),
    .in7(br4_8_a), .out(BusA), .sel(RS__A[4:2]));
  Multiplexer #(.select(3), .width(32), .enable("false")) multiplexer_2 (
    .in0(br4_1_b), .in1(br4_2_b), .in2(br4_3_b), .in3(br4_4_b), .in4(br4_5_b), .in5(br4_6_b), .in6(br4_7_b),
    .in7(br4_8_b), .out(BusB), .sel(RT_B[4:2]));
endmodule

module MULTIPLEXOR_4_1 (
  input  E0,
  input  E1,
  input  E2,
  input  E3,
  input  in_5,
  input  in_6,
  output out_7
);

  wire and_1_out, and_2_out, and_3_out, and_4_out, not_1_out, not_2_out, not_3_out;

  not not_1 (not_1_out, in_5);
  not not_2 (not_2_out, in_6);
  not not_3 (not_3_out, in_6);
  and and_1 (and_1_out, E0, not_1_out, not_2_out);
  and and_2 (and_2_out, E1, not_1_out, in_6);
  and and_3 (and_3_out, E2, in_5, not_3_out);
  and and_4 (and_4_out, E3, in_5, in_6);
  or or_1 (out_7, and_1_out, and_2_out, and_3_out, and_4_out);

  // Notes on the sheet:
  //   8PS
  //   S1
  //   8PS
  //   8PS
  //   S0
  //   25PS
  //   25PS
  //   25PS
  //   25PS
  //   25PS
  //   Camino control salida = D.NOT + D.AND = 8ps + 25ps + 25ps= 58ps 
  //   Camino datos salida = D.AND + D.OR = 25ps + 25ps = 50ps
  //   CAMINO CRÍTICO = 58ps
endmodule

module BR4 (
  input  [1:0] RS,
  input  CLK,
  input  Reset,
  input  [31:0] DATA,
  input  RegWR,
  input  [1:0] RD,
  input  [1:0] RT,
  output [31:0] A,
  output [31:0] B
);

  wire decoder_1_out0, decoder_1_out1, decoder_1_out2, decoder_1_out3;
  wire [31:0] register_1_q, register_2_q, register_3_q, register_4_q;

  Decoder #(.select(2), .disabled(0)) decoder_1 (
    .out0(decoder_1_out0), .out1(decoder_1_out1), .out2(decoder_1_out2), .out3(decoder_1_out3), .sel(RD),
    .en(RegWR));
  Register #(.width(32)) register_1 (.D(DATA), .en(decoder_1_out0), .Q(register_1_q), .clk(CLK), .clr(Reset));
  Register #(.width(32)) register_2 (.D(DATA), .en(decoder_1_out1), .Q(register_2_q), .clk(CLK), .clr(Reset));
  Register #(.width(32)) register_3 (.D(DATA), .en(decoder_1_out2), .Q(register_3_q), .clk(CLK), .clr(Reset));
  Register #(.width(32)) register_4 (.D(DATA), .en(decoder_1_out3), .Q(register_4_q), .clk(CLK), .clr(Reset));
  Multiplexer #(.select(2), .width(32), .enable("false")) multiplexer_1 (
    .in0(register_1_q), .in1(register_2_q), .in2(register_3_q), .in3(register_4_q), .out(A), .sel(RS));
  Multiplexer #(.select(2), .width(32), .enable("false")) multiplexer_2 (
    .in0(register_1_q), .in1(register_2_q), .in2(register_3_q), .in3(register_4_q), .out(B), .sel(RT));
endmodule

module MULTIPLEXOR_8_1 (
  input  _0,
  input  _1,
  input  _2,
  input  _3,
  input  _4,
  input  _5,
  input  _6,
  input  _7,
  input  S2,
  input  S1,
  input  S0,
  input  E,
  output out_13
);

  wire _25PS_2_out, _25PS_3_out, _25PS_4_out, _25PS_5_out, _25PS_7_out, _25PS_8_out, _25PS_9_out, _25PS_out,
       not_1_out, not_2_out, not_3_out, not_4_out, not_5_out, not_6_out;

  not not_1 (not_1_out, S2);
  not not_2 (not_2_out, S1);
  not not_3 (not_3_out, S0);
  not not_4 (not_4_out, not_1_out);
  not not_5 (not_5_out, not_2_out);
  not not_6 (not_6_out, not_3_out);
  and _25PS (_25PS_out, _0, not_1_out, not_2_out, not_3_out, E);
  and _25PS_2 (_25PS_2_out, _1, not_1_out, not_2_out, not_6_out, E);
  and _25PS_3 (_25PS_3_out, _2, not_1_out, not_5_out, not_3_out, E);
  and _25PS_4 (_25PS_4_out, _3, not_1_out, not_5_out, not_6_out, E);
  and _25PS_5 (_25PS_5_out, _4, not_4_out, not_2_out, not_3_out, E);
  or _25PS_6 (out_13, _25PS_out, _25PS_2_out, _25PS_3_out, _25PS_4_out, _25PS_5_out, _25PS_7_out, _25PS_8_out, _25PS_9_out);
  and _25PS_7 (_25PS_7_out, _5, not_4_out, not_2_out, not_6_out, E);
  and _25PS_8 (_25PS_8_out, _6, not_4_out, not_5_out, not_3_out, E);
  and _25PS_9 (_25PS_9_out, _7, not_4_out, not_5_out, not_6_out, E);

  // Notes on the sheet:
  //   8PS
  //   8PS
  //   8PS
  //   8PS
  //   8PS
  //   8PS
  //   CAMINO CRÍTICO =66ps
  //   Camino desde datos a salida = D.AND + D.OR = 25ps + 25ps = 50ps
  //   EN "1" ATRAVIESA LAS 2 PUERTAS OR
  //   Camino desde control a salida = D.Not + D.Not + D.AND + D.OR = 8ps + 8ps + 25ps + 25ps = 66ps
endmodule

module DECODIFICADOR_2_4 (
  input  A0,
  input  _1,
  output S0,
  output S1,
  output S2,
  output S3
);

  wire not_1_out, not_2_out;

  not not_1 (not_1_out, A0);
  not not_2 (not_2_out, _1);
  and _25PS (S0, not_1_out, not_2_out);
  and _25PS_2 (S1, A0, not_2_out);
  and _25PS_3 (S2, _1, not_1_out);
  and _25PS_4 (S3, _1, A0);

  // Notes on the sheet:
  //   A
  //   8PS
  //   8PS
  //   CAMINO CRÍTICO = 8ps + 25ps = 33ps
endmodule

module DECODIFICADOR_3_8 (
  input  A0,
  input  A1,
  input  A2,
  output S0,
  output S1,
  output S2,
  output S3,
  output S4,
  output S5,
  output S6,
  output S7
);

  wire not_1_out, not_2_out, not_3_out;

  not not_1 (not_1_out, A0);
  not not_2 (not_2_out, A1);
  not not_3 (not_3_out, A2);
  and _25PS (S0, not_1_out, not_2_out, not_3_out);
  and _25PS_2 (S1, A0, not_2_out, not_3_out);
  and _25PS_3 (S2, not_1_out, A1, not_3_out);
  and _25PS_4 (S3, A0, A1, not_3_out);
  and _25PS_5 (S4, not_1_out, not_2_out, A2);
  and _25PS_6 (S5, A0, not_2_out, A2);
  and _25PS_7 (S6, not_1_out, A1, A2);
  and _25PS_8 (S7, A0, A1, A2);

  // Notes on the sheet:
  //   8PS
  //   8PS
  //   8PS
  //   CAMINO CRÍTICO = 8ps + 25ps = 33ps
endmodule

module MONOCICLO (
  input  CLK,
  input  Reset
);

  wire Mux2;
  wire [3:0] counter_1_q;
  wire [31:0] adder_1_out, bit_extender_1_out, br32_1_busa, br32_1_busb, Data, rom_1_data;

  Counter #(.width(4), .max('hf)) counter_1 (
    .count(1'b1), .Q(counter_1_q), .clk(CLK), .clr(Reset));  // open: load, D, carry
  ROM #(.addrWidth(4), .dataWidth(32)) rom_1 (
    .addr(counter_1_q), .data({rom_1_data[31:27], Mux2, rom_1_data[25:0]}), .sel(1'b1));
  assign bit_extender_1_out = {{16{1'b0}}, rom_1_data[15:0]};  // Bit_Extender bit_extender_1
  BR32 br32_1 (
    .RS__A(rom_1_data[15:11]), .DATA(Data), .RegWR(1'b1), .RD(rom_1_data[25:21]), .RT_B(rom_1_data[20:16]),
    .BusA(br32_1_busa), .BusB(br32_1_busb), .Reset(Reset), .CLK(CLK));
  Adder #(.width(32)) adder_1 (.a(br32_1_busa), .b(br32_1_busb), .out(adder_1_out));  // open: cin, cout
  Multiplexer #(.width(32), .enable("false")) multiplexer_1 (
    .in0(adder_1_out), .in1(bit_extender_1_out), .out(Data), .sel(Mux2));

  // Notes on the sheet:
  //   contents of rom_1 (hex, n*v repeats v):
  //   0 4000007 4200008 4400000 4600003 4800003 4a00006 c03000 c13000 c23000 c33000 c43000 c53000
  //   (16-20)
  //   (11-15)
  //   (21-25)
  //   INMEDIATO (0-15)
endmodule

module CONTROL_MONOCICLO (
  input  OP,
  output Mux1,
  output RegWr,
  output Mux2
);

  not not_1 (Mux1, OP);
  or or_1 (RegWr, Mux1, OP);

  assign Mux2 = OP;
endmodule

module MULTICICLO (
  input  in_1,
  input  Reset
);

  wire Mux1, PC, RegWr;
  wire [2:0] rom_2_data, UC;
  wire [3:0] counter_1_q;
  wire [31:0] adder_1_out, bit_extender_1_out, br32_1_busa, br32_1_busb, Data, register_2_q, register_3_q,
       register_4_q, rom_1_data;

  Counter #(.width(4), .max('hf)) counter_1 (
    .count(1'b1), .Q(counter_1_q), .clk(PC), .clr(Reset));  // open: load, D, carry
  ROM #(.addrWidth(4), .dataWidth(32)) rom_1 (.addr(counter_1_q), .data(rom_1_data), .sel(1'b1));
  ROM #(.addrWidth(4), .dataWidth(6)) rom_2 (
    .addr({rom_1_data[26], UC}), .data({Mux1, RegWr, PC, rom_2_data}), .sel(1'b1));
  assign bit_extender_1_out = {{16{1'b0}}, rom_1_data[15:0]};  // Bit_Extender bit_extender_1
  BR32 br32_1 (
    .RS__A(rom_1_data[15:11]), .DATA(Data), .RegWR(RegWr), .RD(rom_1_data[25:21]), .RT_B(rom_1_data[20:16]),
    .BusA(br32_1_busa), .BusB(br32_1_busb), .Reset(Reset), .CLK(in_1));
  Register #(.width(3)) register_1 (.D(rom_2_data), .en(1'b1), .Q(UC), .clk(in_1), .clr(Reset));
  Register #(.width(32)) register_2 (.D(br32_1_busa), .en(1'b1), .Q(register_2_q), .clk(in_1), .clr(Reset));
  Register #(.width(32)) register_3 (.D(br32_1_busb), .en(1'b1), .Q(register_3_q), .clk(in_1), .clr(Reset));
  Adder #(.width(32)) adder_1 (.a(register_2_q), .b(register_3_q), .out(adder_1_out));  // open: cin, cout
  Register #(.width(32)) register_4 (.D(adder_1_out), .en(1'b1), .Q(register_4_q), .clk(in_1), .clr(Reset));
  Multiplexer #(.width(32), .enable("false")) multiplexer_1 (
    .in0(register_4_q), .in1(bit_extender_1_out), .out(Data), .sel(Mux1));

  // Other names for the same wires on the sheet: CLK = in_1

  // Notes on the sheet:
  //   contents of rom_1 (hex, n*v repeats v):
  //   0 4000007 4200008 4400000 4600003 4800003 4a00006 c03000 c13000 c23000 c33000 c43000 c53000
  //   (16-20)
  //   (11-15)
  //   (21-25)
  //   INMEDIATO (0-15)
  //   contents of rom_2 (hex, n*v repeats v):
  //   2 18 3 4 18 0 0 0 1 38 3 4 38
endmodule

module MULTIPLEXOR_2_1 (
  input  [31:0] in_1,
  input  [31:0] in_2,
  input  in_3,
  output [31:0] out_4
);

  wire [31:0] and_1_out, and_2_out, bit_extender_1_out, not_1_out;

  assign bit_extender_1_out = {{31{1'b0}}, in_3};  // Bit_Extender bit_extender_1
  assign not_1_out = ~bit_extender_1_out;  // NOT_Gate not_1, 32 bits wide
  assign and_1_out = in_1 & not_1_out;  // AND_Gate and_1, 32 bits wide
  assign and_2_out = in_2 & bit_extender_1_out;  // AND_Gate and_2, 32 bits wide
  assign out_4 = and_1_out | and_2_out;  // OR_Gate or_1, 32 bits wide

  // Notes on the sheet:
  //   * Camino crítico = control = 75ps
  //   * Datos = DelayAND +DelayOR = 30PS + 30PS = 60PS
  //   * Control = DelayExtensorSigno + DelayNot + DelayAND + DelayOR = 10ps + 5ps + 30ps + 30ps = 75ps 
endmodule
