// Logisim project Practica4.circ as structural Verilog: 4 circuits, main circuit MULTICICLO
module BR32 (
  input  CLK,
  input  Reset,
  input  [31:0] DATA,
  input  RegWR,
  input  [4:0] RS__A,
  input  [4:0] RD,
  input  [4:0] RT_B,
  output [31:0] BusA,
  output [31:0] BusB
);

  wire decoder_1_out0, decoder_1_out1, decoder_1_out2, decoder_1_out3, decoder_1_out4, decoder_1_out5,
       decoder_1_out6, decoder_1_out7;
  wire [31:0] br4_1_a, br4_1_b, br4_2_a, br4_2_b, br4_3_a, br4_3_b, br4_4_a, br4_4_b, br4_5_a, br4_5_b,
       br4_6_a, br4_6_b, br4_7_a, br4_7_b, br4_8_a, br4_8_b;

  Decoder #(.select(3), .disabled(0)) decoder_1 (
    .out0(decoder_1_out0), .out1(decoder_1_out1), .out2(decoder_1_out2), .out3(decoder_1_out3),
    .out4(decoder_1_out4), .out5(decoder_1_out5), .out6(decoder_1_out6), .out7(decoder_1_out7),
    .sel(RD[4:2]), .en(RegWR));
  BR4 br4_1 (
    .DATA(DATA), .RegWR(decoder_1_out0), .RD(RD[1:0]), .A(br4_1_a), .B(br4_1_b), .CLK(CLK), .Reset(Reset),
    .RS(RS__A[1:0]), .RT(RT_B[1:0]));
  BR4 br4_2 (
    .DATA(DATA), .RegWR(decoder_1_out1), .RD(RD[1:0]), .A(br4_2_a), .B(br4_2_b), .CLK(CLK), .Reset(Reset),
    .RS(RS__A[1:0]), .RT(RT_B[1:0]));
  BR4 br4_3 (
    .DATA(DATA), .RegWR(decoder_1_out2), .RD(RD[1:0]), .A(br4_3_a), .B(br4_3_b), .CLK(CLK), .Reset(Reset),
    .RS(RS__A[1:0]), .RT(RT_B[1:0]));
  BR4 br4_4 (
    .DATA(DATA), .RegWR(decoder_1_out3), .RD(RD[1:0]), .A(br4_4_a), .B(br4_4_b), .CLK(CLK), .Reset(Reset),
    .RS(RS__A[1:0]), .RT(RT_B[1:0]));
  BR4 br4_5 (
    .DATA(DATA), .RegWR(decoder_1_out4), .RD(RD[1:0]), .A(br4_5_a), .B(br4_5_b), .CLK(CLK), .Reset(Reset),
    .RS(RS__A[1:0]), .RT(RT_B[1:0]));
  BR4 br4_6 (
    .DATA(DATA), .RegWR(decoder_1_out5), .RD(RD[1:0]), .A(br4_6_a), .B(br4_6_b), .CLK(CLK), .Reset(Reset),
    .RS(RS__A[1:0]), .RT(RT_B[1:0]));
  BR4 br4_7 (
    .DATA(DATA), .RegWR(decoder_1_out6), .RD(RD[1:0]), .A(br4_7_a), .B(br4_7_b), .Reset(Reset),
    .RS(RS__A[1:0]), .RT(RT_B[1:0]));  // open: CLK
  BR4 br4_8 (
    .DATA(DATA), .RegWR(decoder_1_out7), .RD(RD[1:0]), .A(br4_8_a), .B(br4_8_b), .CLK(CLK), .Reset(Reset),
    .RS(RS__A[1:0]), .RT(RT_B[1:0]));
  Multiplexer #(.select(3), .width(32), .enable("false")) multiplexer_1 (
    .in0(br4_1_a), .in1(br4_2_a), .in2(br4_3_a), .in3(br4_4_a), .in4(br4_5_a), .in5(br4_6_a), .in6(br4_7_a),
    .in7(br4_8_a), .out(BusA), .sel(RS__A[4:2]));
  Multiplexer #(.select(3), .width(32), .enable("false")) multiplexer_2 (
    .in0(br4_1_b), .in1(br4_2_b), .in2(br4_3_b), .in3(br4_4_b), .in4(br4_5_b), .in5(br4_6_b), .in6(br4_7_b),
    .in7(br4_8_b), .out(BusB), .sel(RT_B[4:2]));
endmodule

module BR4 (
  input  [1:0] RS,
  input  CLK,
  input  Reset,
  input  [31:0] DATA,
  input  RegWR,
  input  [1:0] RD,
  input  [1:0] RT,
  output [31:0] A,
  output [31:0] B
);

  wire decoder_1_out0, decoder_1_out1, decoder_1_out2, decoder_1_out3;
  wire [31:0] register_1_q, register_2_q, register_3_q, register_4_q;

  Decoder #(.select(2), .disabled(0)) decoder_1 (
    .out0(decoder_1_out0), .out1(decoder_1_out1), .out2(decoder_1_out2), .out3(decoder_1_out3), .sel(RD),
    .en(RegWR));
  Register #(.width(32)) register_1 (.D(DATA), .en(decoder_1_out0), .Q(register_1_q), .clk(CLK), .clr(Reset));
  Register #(.width(32)) register_2 (.D(DATA), .en(decoder_1_out1), .Q(register_2_q), .clk(CLK), .clr(Reset));
  Register #(.width(32)) register_3 (.D(DATA), .en(decoder_1_out2), .Q(register_3_q), .clk(CLK), .clr(Reset));
  Register #(.width(32)) register_4 (.D(DATA), .en(decoder_1_out3), .Q(register_4_q), .clk(CLK), .clr(Reset));
  Multiplexer #(.select(2), .width(32), .enable("false")) multiplexer_1 (
    .in0(register_1_q), .in1(register_2_q), .in2(register_3_q), .in3(register_4_q), .out(A), .sel(RS));
  Multiplexer #(.select(2), .width(32), .enable("false")) multiplexer_2 (
    .in0(register_1_q), .in1(register_2_q), .in2(register_3_q), .in3(register_4_q), .out(B), .sel(RT));
endmodule

module MULTICICLO (
  input  Reset
);

  wire AND, and_1_out, BEQ, CLK, habilitarMEN, MuxPC, MuxRW, not_1_out, PC, RD_WR, RegWr;
  wire [1:0] MuxBR32;
  wire [2:0] CodOperacion;
  wire [3:0] rom_2_data, SigEstado;
  wire [4:0] multiplexer_1_out, register_1_q_2, register_1_q_3;
  wire [15:0] counter_1_q, Mux1;
  wire [31:0] adder_1_out, br32_1_busa, br32_1_busb, Data, DATA_MEM, MEM, ram_1_data, register_3_q,
       rom_1_data, SigExt, SUMADOR;
  wire [31:29] register_1_q;

  not not_1 (not_1_out, MuxPC);
  and and_1 (and_1_out, PC, not_1_out);
  Counter #(.width(16), .max('hffff)) counter_1 (
    .load(MuxPC), .D(Mux1), .count(and_1_out), .Q(counter_1_q), .clk(CLK), .clr(Reset));  // open: carry
  Clock clock_1 (.out(CLK));
  ROM #(.addrWidth(16), .dataWidth(32)) rom_1 (.addr(counter_1_q), .data(rom_1_data), .sel(1'b1));
  Register #(.width(32)) register_1 (
    .D(rom_1_data), .en(1'b1), .Q({register_1_q, CodOperacion, register_1_q_2, register_1_q_3, Mux1}),
    .clk(CLK), .clr(Reset));
  ROM #(.addrWidth(7), .dataWidth(12)) rom_2 (
    .addr({CodOperacion, SigEstado}), .data({BEQ, MuxRW, MuxBR32, habilitarMEN, RD_WR, RegWr, PC, rom_2_data}));  // open: sel
  Multiplexer #(.width(5), .enable("false")) multiplexer_1 (
    .in0(register_1_q_3), .in1(Mux1[15:11]), .out(multiplexer_1_out), .sel(MuxRW));
  assign SigExt = {{16{1'b0}}, Mux1};  // Bit_Extender bit_extender_1
  BR32 br32_1 (
    .RS__A(register_1_q_2), .DATA(Data), .RegWR(RegWr), .RD(multiplexer_1_out), .RT_B(register_1_q_3),
    .BusA(br32_1_busa), .BusB(br32_1_busb), .Reset(Reset), .CLK(CLK));
  Register #(.width(4)) register_2 (.D(rom_2_data), .en(1'b1), .Q(SigEstado), .clk(CLK), .clr(Reset));
  Register #(.width(32)) register_3 (.D(br32_1_busa), .en(1'b1), .Q(register_3_q), .clk(CLK), .clr(Reset));
  Register #(.width(32)) register_4 (.D(br32_1_busb), .en(1'b1), .Q(DATA_MEM), .clk(CLK), .clr(Reset));
  Comparator #(.width(32)) comparator_1 (.a(register_3_q), .b(DATA_MEM), .eq(AND));  // open: gt, lt
  and and_2 (MuxPC, BEQ, AND);
  Adder #(.width(32)) adder_1 (.a(register_3_q), .b(DATA_MEM), .out(adder_1_out));  // open: cin, cout
  RAM #(.addrWidth(16), .dataWidth(32), .bus("separate")) ram_1 (
    .addr(register_3_q[15:0]), .din(DATA_MEM), .data(ram_1_data), .str(RD_WR), .sel(habilitarMEN), .clk(CLK),
    .ld(habilitarMEN));  // open: clr
  Register #(.width(32)) register_5 (.D(ram_1_data), .en(1'b1), .Q(MEM), .clk(CLK), .clr(Reset));
  Register #(.width(32)) register_6 (.D(adder_1_out), .en(1'b1), .Q(SUMADOR), .clk(CLK), .clr(Reset));
  Multiplexer #(.select(2), .width(32), .enable("false")) multiplexer_2 (
    .in0(SUMADOR), .in1(MEM), .in2(SigExt), .out(Data), .sel(MuxBR32));  // open: in3

  // Notes on the sheet:
  //   PC
  //   IR
  //   contents of rom_1 (hex, n*v repeats v):
  //   4000001 4020006 4030007 8240000 14200800 14a42800 10220008 10000003 c650000
  //   (21-25)
  //   (16-20)
  //   (11-15)
  //   INMEDIATO (0-15)
  //   contents of rom_2 (hex, n*v repeats v):
  //   16*0 8 7*0 230 7*0 1 4 0 0 85 170 10*0 1 6 4*0 d0 9*0 1 7 5*0 810 8*0 1 2 3 430
endmodule

module SEGMENTADO (
  input  Reset
);

  wire AND, AND2, and_1_out, BEQ, CLK, habilitarMEN, MuxPC, MuxRW, not_1_out, RD_WR, RegWr;
  wire [1:0] MuxBR32;
  wire [2:0] EX_MEN_q, ROM;
  wire [4:0] EX_MEN_8_q, multiplexer_1_out, register_1_q_3, RW, RW1, RW2;
  wire [5:0] ID_EX_q;
  wire [6:0] rom_2_data;
  wire [9:0] ID_EX_3_q;
  wire [10:0] register_1_q_2;
  wire [15:0] counter_1_q, ID_EX_2_q, Mux1;
  wire [31:0] A, adder_1_out, B, bit_extender_1_out, br32_1_busa, br32_1_busb, Data, EX_MEN_2_q, EX_MEN_3_q,
       EX_MEN_4_q, EX_MEN_5_q, MEM, ram_1_data, register_4_q, rom_1_data, SigExt, SUMADOR;
  wire [31:29] register_1_q;

  and and_1 (and_1_out, 1'b1, not_1_out);
  not not_1 (not_1_out, MuxPC);
  Counter #(.width(16), .max('hffff)) counter_1 (
    .load(MuxPC), .D(Mux1), .count(and_1_out), .Q(counter_1_q), .clk(CLK), .clr(Reset));  // open: carry
  Clock clock_1 (.out(CLK));
  ROM #(.addrWidth(16), .dataWidth(32)) rom_1 (.addr(counter_1_q), .data(rom_1_data), .sel(1'b1));
  Register #(.width(32)) register_1 (
    .D(rom_1_data), .en(1'b1), .Q({register_1_q, ROM, register_1_q_3, RW1, RW2, register_1_q_2}), .clk(CLK),
    .clr(Reset));
  ROM #(.addrWidth(3), .dataWidth(7)) rom_2 (.addr(ROM), .data(rom_2_data));  // open: sel
  assign bit_extender_1_out = {{16{1'b0}}, {RW2, register_1_q_2}};  // Bit_Extender bit_extender_1
  BR32 br32_1 (
    .RS__A(register_1_q_3), .DATA(Data), .RegWR(RegWr), .RD(RW), .RT_B(RW1), .BusA(br32_1_busa),
    .BusB(br32_1_busb), .Reset(Reset), .CLK(CLK));
  Register #(.width(7)) ID_EX (.D(rom_2_data), .en(1'b1), .Q({MuxRW, ID_EX_q}), .clk(CLK), .clr(Reset));
  Register #(.width(32)) register_2 (.D(br32_1_busa), .en(1'b1), .Q(A), .clk(CLK), .clr(Reset));
  Register #(.width(32)) register_3 (.D(br32_1_busb), .en(1'b1), .Q(B), .clk(CLK), .clr(Reset));
  Register #(.width(32)) register_4 (.D(bit_extender_1_out), .en(1'b1), .Q(register_4_q), .clk(CLK), .clr(Reset));
  Register #(.width(16)) ID_EX_2 (.D({RW2, register_1_q_2}), .en(1'b1), .Q(ID_EX_2_q), .clk(CLK), .clr(Reset));
  Register #(.width(10)) ID_EX_3 (.D({RW2, RW1}), .en(1'b1), .Q(ID_EX_3_q), .clk(CLK), .clr(Reset));
  Multiplexer #(.width(5), .enable("false")) multiplexer_1 (
    .in0(ID_EX_3_q[4:0]), .in1(ID_EX_3_q[9:5]), .out(multiplexer_1_out), .sel(MuxRW));
  Adder #(.width(32)) adder_1 (.a(A), .b(B), .out(adder_1_out));  // open: cin, cout
  Comparator #(.width(32)) comparator_1 (.a(A), .b(B), .eq(AND));  // open: gt, lt
  Register #(.width(6)) EX_MEN (
    .D(ID_EX_q), .en(1'b1), .Q({BEQ, habilitarMEN, RD_WR, EX_MEN_q}), .clk(CLK), .clr(Reset));
  Register #(.width(32)) EX_MEN_2 (.D(A), .en(1'b1), .Q(EX_MEN_2_q), .clk(CLK), .clr(Reset));
  Register #(.width(32)) EX_MEN_3 (.D(B), .en(1'b1), .Q(EX_MEN_3_q), .clk(CLK), .clr(Reset));
  Register #(.width(32)) EX_MEN_4 (.D(adder_1_out), .en(1'b1), .Q(EX_MEN_4_q), .clk(CLK), .clr(Reset));
  Register #(.width(32)) EX_MEN_5 (.D(register_4_q), .en(1'b1), .Q(EX_MEN_5_q), .clk(CLK), .clr(Reset));
  Register #(.width(1)) EX_MEN_6 (.D(AND), .en(1'b1), .Q(AND2), .clk(CLK), .clr(Reset));
  Register #(.width(16)) EX_MEN_7 (.D(ID_EX_2_q), .en(1'b1), .Q(Mux1), .clk(CLK), .clr(Reset));
  Register #(.width(5)) EX_MEN_8 (.D(multiplexer_1_out), .en(1'b1), .Q(EX_MEN_8_q), .clk(CLK), .clr(Reset));
  RAM #(.addrWidth(16), .dataWidth(32), .bus("separate")) ram_1 (
    .addr(EX_MEN_2_q[15:0]), .din(EX_MEN_3_q), .data(ram_1_data), .str(RD_WR), .sel(habilitarMEN), .clk(CLK),
    .ld(habilitarMEN));  // open: clr
  and and_2 (MuxPC, BEQ, AND2);
  Register #(.width(3)) MEN_WB (.D(EX_MEN_q), .en(1'b1), .Q({MuxBR32, RegWr}), .clk(CLK), .clr(Reset));
  Register #(.width(32)) MEN_WB_2 (.D(ram_1_data), .en(1'b1), .Q(MEM), .clk(CLK), .clr(Reset));
  Register #(.width(32)) MEN_WB_3 (.D(EX_MEN_4_q), .en(1'b1), .Q(SUMADOR), .clk(CLK), .clr(Reset));
  Register #(.width(32)) MEN_WB_4 (.D(EX_MEN_5_q), .en(1'b1), .Q(SigExt), .clk(CLK), .clr(Reset));
  Register #(.width(5)) MEN_WB_5 (.D(EX_MEN_8_q), .en(1'b1), .Q(RW), .clk(CLK), .clr(Reset));
  Multiplexer #(.select(2), .width(32), .enable("false")) multiplexer_2 (
    .in0(SUMADOR), .in1(MEM), .in2(SigExt), .out(Data), .sel(MuxBR32));  // open: in3

  // Notes on the sheet:
  //   PC
  //   Memoria Instucciones
  //   contents of rom_1 (hex, n*v repeats v):
  //   4000001 4020006 4030007 18000000 8240000 14200800 18000000 18000000 14a42800 10220011 18000000
  //   18000000 18000000 10000003 18000000 18000000 18000000 c650000
  //   IF/ID
  //   (21-25)
  //   (16-20)
  //   (11-15)
  //   INMEDIATO (0-15)
  //   contents of rom_2 (hex, n*v repeats v):
  //   0 5 13 18 20 41
  //   DIR.SALTO CONDICIONAL
  //   UNIDAD DE CONTROL
  //   REGISTRO DESTINO (RW)
  //   ID/EX
  //   ID/EX
  //   ID/EX
  //   out = 0 escritura
endmodule
